# Fritzing sketch _ORIGINAL (saved by Fritzing 0.9.2b)
circuit board: 9.39cm x 9.39cm
breadboards: 1

parts:
  S1 = Toggle Switch [package=THT]
  C25 = Ceramic Capacitor [package="0603 [SMD, multilayer]"]
  U6 = QRD1114 [package=qrd1114]
  C26 = Ceramic Capacitor [capacitance=0.1µF package="0603 [SMD, multilayer]"]
  R20 = Resistor [tolerance=±5% resistance=220 package="0603 [SMD]"]
  R16 = Resistor [tolerance=±5% resistance=220 package="0603 [SMD]"]
  AVR_ISP_programmer = shrouded pin header, 6 pins [form="♂ (shrouded male)"]
  C5 = Ceramic Capacitor [capacitance=1µF voltage=10V package="0603 [SMD, multilayer]"]
  L1_2_2uH = Inductors [package=1210]
  C1 = Ceramic Capacitor [capacitance=10µF voltage=10V package="0603 [SMD, multilayer]"]
  U8 = QRD1114 [package=qrd1114]
  U7 = QRD1114 [package=qrd1114]
  R12 = Resistor [tolerance=±5% resistance=220 package="0603 [SMD]"]
  C2 = Ceramic Capacitor [capacitance=0.1µF voltage=10V package="0603 [SMD, multilayer]"]
  C6 = Ceramic Capacitor [capacitance=0.1µF voltage=10V package="0603 [SMD, multilayer]"]
  R21 = Resistor [tolerance=±5% resistance=220 package="0603 [SMD]"]
  Power_plug1 = Power plug
  R16_2 = Resistor [tolerance=±5% resistance=1k package="0603 [SMD]"]
  Motors = Header 4 [package=molex-1x4_lock]
  B1 = Battery
  C4 = Ceramic Capacitor [capacitance=10µF voltage=10V package="0603 [SMD, multilayer]"]
  C21 = Ceramic Capacitor [package="0603 [SMD, multilayer]"]
  LED1 = smd LED [color="Green (570nm)" package="0805 [SMD]"]
  R33 = Resistor [tolerance=±5% resistance=1k package="0603 [SMD]"]
  R15 = Resistor [tolerance=±5% resistance=10k package="0603 [SMD]"]
  U1 = Voltage Regulator - 5V [package="TO220 [THT]"]
  C23 = Ceramic Capacitor [package="0603 [SMD, multilayer]"]
  R14 = Resistor [tolerance=±5% resistance=220 package="0603 [SMD]"]
  B2 = Battery
  D5 = smd LED [color="Blue (525nm)" package="0603 [SMD]"]
  U4 = QRD1114 [package=qrd1114]
  C22 = Ceramic Capacitor [package="0603 [SMD, multilayer]"]
  Q1_reverse_protection = Basic FET P-Channel [package="TO220 [THT]"]
  R13 = Resistor [tolerance=±5% resistance=220 package="0603 [SMD]"]
  R23 = Resistor [tolerance=±5% resistance=220 package="0603 [SMD]"]
  C24 = Ceramic Capacitor [package="0603 [SMD, multilayer]"]
  R15_2 = Resistor [tolerance=±5% resistance=220 package="0603 [SMD]"]
  U5 = QRD1114 [package=qrd1114]
  D6 = Zener Diode [part_number=1N4732A breakdown_voltage=5.1V package="Melf DO-213 AB [SMD]"]
  L2_10uH = Inductors [package=1210]
  U2 = TPS61200 [package=qfn-10_pad]
  ATMEGA_168_tqfp32_8mm = ATMEGA168 [package=tqfp]
  S2_RESET = Pushbutton [package=THT]
  Q4 = Basic FET P-Channel [package="TO220 [THT]"]
  C3 = Ceramic Capacitor [capacitance=0.1µF voltage=10V package="0603 [SMD, multilayer]"]
  C18 = Ceramic Capacitor [capacitance=0.1µF voltage=10V package="0603 [SMD, multilayer]"]
  C32 = Ceramic Capacitor [capacitance=0.1µF package="0603 [SMD, multilayer]"]
  R31 = Resistor [tolerance=±5% resistance=22k package="0603 [SMD]"]
  R30 = Resistor [tolerance=±5% resistance=22k package="0603 [SMD]"]
  R32 = Resistor [tolerance=±5% resistance=22k package="0603 [SMD]"]
  J6 = single row smd female pin header, 2 pins [form="♀ (female)"]
  J4 = single row smd female pin header, 2 pins [form="♀ (female)"]
  R16_10k = TRIMPOT [package=trimpot-3mm]
  XTAL1 = Crystal [frequency="20 MHz" package=SMD]
  TB6612FNG = Motor Driver 1A Dual TB6612FNG

nets:
  N1: S1.COM, Q1_reverse_protection.source
  N2: S1.L2, L1_2_2uH.1, C1.1, C2.1, R16_2.Pin_0, U2.VIN, U2.EN, U2.UVLO, R31.Pin_1, R30.Pin_1
  N3: C25.0, R16.Pin_1, U8.E
  VCC: C25.1, AVR_ISP_programmer.pin2, C21.1, R15.Pin_0, U1.output_voltage, C23.1, C22.1, R23.Pin_1, C24.1, L2_10uH.1, ATMEGA_168_tqfp32_8mm.VCC, R16_10k.CW, TB6612FNG.VCC, TB6612FNG.PWMA, TB6612FNG.PWMB
  N4: U6.E, C23.0, R14.Pin_1
  GND: U6.C, C26.0, AVR_ISP_programmer.pin6, U8.C, U7.C, U4.C, U5.C, ATMEGA_168_tqfp32_8mm.GND, ATMEGA_168_tqfp32_8mm.AGND, S2_RESET.leg0, Q4.drain, C32.0, R32.Pin_0, R16_10k.CCW, TB6612FNG.GND
  N5: U6.A, U5.K
  N6: U6.K, U7.A
  N7: C26.1, AVR_ISP_programmer.pin5, R15.Pin_1, ATMEGA_168_tqfp32_8mm.PC6(_RESET), S2_RESET.leg1, TB6612FNG.STBY
  N8: R20.Pin_0, R21.Pin_0, Q4.source
  N9: R20.Pin_1, U8.K, R21.Pin_1
  N10: R16.Pin_0, ATMEGA_168_tqfp32_8mm.PC4(ADC4_SDA)
  N11: AVR_ISP_programmer.pin1, ATMEGA_168_tqfp32_8mm.PB4(MISO)
  N12: AVR_ISP_programmer.pin3, ATMEGA_168_tqfp32_8mm.PB5(SCK)
  N13: AVR_ISP_programmer.pin4, ATMEGA_168_tqfp32_8mm.PB3(MOSI_OC2), TB6612FNG.AIN1
  GND_2: C5.0, C1.0, C2.0, C6.0, Power_plug1.GND, C4.0, LED1.cathode, U1.GND, B2.-, Q1_reverse_protection.gate, D6.anode, U2.PGND, U2.PS, U2.GND, U2.PAD, C3.0, C18.0
  N14: C5.1, C6.1, C4.1, R33.Pin_0, U1.input_voltage, U4.A, U2.VOUT, U2.FB, TB6612FNG.VM
  N15: L1_2_2uH.2, U2.L
  N16: U8.A, U7.K
  N17: U7.E, C24.0, R15_2.Pin_1
  N18: R12.Pin_0, ATMEGA_168_tqfp32_8mm.PC0(ADC0)
  N19: R12.Pin_1, C21.0, U4.E
  N20: Power_plug1.VCC, B1.+, Q1_reverse_protection.drain
  N21: R16_2.Pin_1, LED1.anode
  N22: Motors.1, TB6612FNG.B02
  N23: Motors.2, TB6612FNG.B01
  N24: Motors.3, TB6612FNG.A02
  N25: Motors.4, TB6612FNG.A01
  N26: B1.-, B2.+
  N27: R33.Pin_1, D5.anode
  N28: R14.Pin_0, ATMEGA_168_tqfp32_8mm.PC2(ADC2)
  N29: D5.cathode, D6.cathode
  N30: U4.K, U5.A
  N31: C22.0, R13.Pin_1, U5.E
  N32: R13.Pin_0, ATMEGA_168_tqfp32_8mm.PC1(ADC1)
  N33: R23.Pin_0, ATMEGA_168_tqfp32_8mm.PC5(ADC5_SCL), Q4.gate
  N34: R15_2.Pin_0, ATMEGA_168_tqfp32_8mm.PC3(ADC3)
  N35: L2_10uH.2, ATMEGA_168_tqfp32_8mm.AVCC, C18.1
  N36: U2.VAUX, C3.1
  N37: ATMEGA_168_tqfp32_8mm.PD3(INT1), TB6612FNG.AIN2
  N38: ATMEGA_168_tqfp32_8mm.PB6(XTAL1_TOSC1), XTAL1.pin_1
  N39: ATMEGA_168_tqfp32_8mm.PB7(XTAL2_TOSC2), XTAL1.pin_0
  N40: ATMEGA_168_tqfp32_8mm.PD5(T1), TB6612FNG.BIN1
  N41: ATMEGA_168_tqfp32_8mm.PD6(AIN0), TB6612FNG.BIN2
  N42: ATMEGA_168_tqfp32_8mm.ADC6, J6.pin1
  N43: ATMEGA_168_tqfp32_8mm.AREF, C32.1
  N44: ATMEGA_168_tqfp32_8mm.ADC7, J4.pin1
  N45: R31.Pin_0, R30.Pin_0, R32.Pin_1, J6.pin2
  N46: J4.pin2, R16_10k.WIPER

custom parts:
  Ceramic Capacitor: 0.01 nF multilayered Ceramic Capacitor
