# Fritzing sketch schematic_v0.1 (saved by Fritzing 0.9.2b)
breadboards: 1

parts:
  part = Arduino Nano (Rev3.0) (ICSP)
  DC/DC_Converter_0_8-20VDC/1_8A = Voltage Regulator - Variable [package="TO220 [THT]"]
  CAR_SUPPLY_~12-14VDC = DC Power [voltage=12V]
  BUTTON_KONST = Round Pushbutton
  R1 = Resistor [tolerance=±5% resistance=10 package="0603 [SMD]"]
  BUTTON_ABRUF = Round Pushbutton
  BUTTON_TEMPO = Round Pushbutton
  R2 = Resistor [tolerance=±5% resistance=10 package="0603 [SMD]"]
  R3 = Resistor [tolerance=±5% resistance=10 package="0603 [SMD]"]
  JV-5S-KT_5VDC_250VAC/5A = RELAY [package=relay-g5q]
  D1 = Rectifier Diode [part_number=1N4001 package="Melf DO-213 AB [SMD]"]
  BC547 = TRANSISTOR_NPN_2 [package=to-92]
  4N25 = Optocoupler [package=THT]
  JV-5S-KT_5VDC_250VAC/5A_2 = RELAY [package=relay-g5q]
  D2 = Rectifier Diode [part_number=1N4001 package="Melf DO-213 AB [SMD]"]
  BC548 = TRANSISTOR_NPN_2 [package=to-92]
  R4 = Resistor [tolerance=±5% resistance=10k package=THT]
  R5 = Resistor [tolerance=±5% resistance=10k package=THT]
  R6 = Resistor [tolerance=±5% resistance=4.7k package=THT]
  D3 = Rectifier Diode [part_number=1N4148 package="Melf DO-213 AB [SMD]"]
  R7 = Resistor [tolerance=±5% resistance=4.7k package=THT]

nets:
  N1: part.GND, R1.Pin_1, R2.Pin_1, R3.Pin_1, BC547.E, 4N25.Pin_4, BC548.E
  N2: part.D2, BUTTON_KONST.leg0, R1.Pin_0
  N3: part.D3, BUTTON_ABRUF.leg0, R2.Pin_0
  N4: part.D4, BUTTON_TEMPO.leg0, R3.Pin_0
  N5: part.D5, R4.Pin_0
  N6: part.D6, R5.Pin_0
  N7: part.D7, 4N25.Pin_5, R6.Pin_1
  N8: part.VIN, DC/DC_Converter_0_8-20VDC/1_8A.OUT
  N9: part.5V, BUTTON_KONST.leg1, BUTTON_ABRUF.leg1, BUTTON_TEMPO.leg1, R6.Pin_0
  N10: DC/DC_Converter_0_8-20VDC/1_8A.IN, CAR_SUPPLY_~12-14VDC.V+, JV-5S-KT_5VDC_250VAC/5A.MAIN, JV-5S-KT_5VDC_250VAC/5A_2.NC
  N11: CAR_SUPPLY_~12-14VDC.V-, 4N25.Pin_2, D3.anode
  N12: JV-5S-KT_5VDC_250VAC/5A.COIL2, D1.anode, BC547.C
  clutch +12VDC: JV-5S-KT_5VDC_250VAC/5A.NO
  N13: JV-5S-KT_5VDC_250VAC/5A.COIL1, D1.cathode
  N14: BC547.B, R4.Pin_1
  N15: 4N25.Pin_1, D3.cathode, R7.Pin_1
  N16: JV-5S-KT_5VDC_250VAC/5A_2.COIL2, D2.anode, BC548.C
  motor +12VDC: JV-5S-KT_5VDC_250VAC/5A_2.NO
  N17: JV-5S-KT_5VDC_250VAC/5A_2.COIL1, D2.cathode
  N18: BC548.B, R5.Pin_1
  break signal +12VDC: R7.Pin_0

notes:
  RELAY_CLUTCH
  RELAY_MOTOR
  BREAK_SIGNAL
